# Fritzing sketch Circuit Diagram (saved by Fritzing 1.0.5)
breadboards: 2

parts:
  Launchpad2 = LaunchPad EK-TM4C123GXL
  L298N1 = L298N DC motor driver
  Power_plug1 = Power plug
  LCD1 = LCD screen
  LCM1602_IIC1 = LCM1602 IIC [part_number="LCM1602 IIC" chip_label="LCM1602 IIC" package="DIP (Dual Inline) [THT]"]
  R1 = Resistor [tolerance=±5% resistance=20000 package="2010 [SMD]"]
  R2 = Resistor [tolerance=±5% resistance=20000 package="2010 [SMD]"]  # not connected
  S1 = Pushbutton [package="[THT]"]
  S2 = Pushbutton [package="[THT]"]
  S3 = Pushbutton [package="[THT]"]
  R3 = Resistor [tolerance=±5% resistance=100 package="0603 [SMD]"]
  R4 = Resistor [tolerance=±5% resistance=100 package="0603 [SMD]"]
  Power_plug2 = Power plug
  R5 = Resistor [tolerance=±5% resistance=100 package="0603 [SMD]"]
  R7 = 220 Ω Resistor [package="0603 [SMD]"]  # not connected
  R6 = 220 Ω Resistor [package="0603 [SMD]"]  # not connected
  RE2 = Rotary Encoder [package=THT]  # not connected
  R8 = Resistor [tolerance=±5% resistance=100 package="0603 [SMD]"]
  M1 = gear-motor
  R13 = Resistor [tolerance=±5% resistance=100 package="0603 [SMD]"]  # not connected
  R14 = Resistor [tolerance=±5% resistance=100 package="0603 [SMD]"]  # not connected
  R15 = Resistor [tolerance=±5% resistance=20000 package="2010 [SMD]"]
  R16 = Resistor [tolerance=±5% resistance=20000 package="2010 [SMD]"]  # not connected
  R18 = Resistor [tolerance=±5% resistance=100 package="0603 [SMD]"]  # not connected
  R19 = Resistor [tolerance=±5% resistance=100 package="0603 [SMD]"]  # not connected
  R20 = Resistor [tolerance=±5% resistance=100 package="0603 [SMD]"]

nets:
  N1: Launchpad2.pin_19, LCM1602_IIC1.SCL
  GND: Launchpad2.pin_22, LCM1602_IIC1.GND, R3.Pin_0, R4.Pin_0, Power_plug2.GND, R5.Pin_1, R8.Pin_0
  N2: Launchpad2.pin_35, S1.Pin_1, S1.Pin_2, R4.Pin_1
  N3: Launchpad2.pin_36, S2.Pin_1, S2.Pin_2, R5.Pin_0
  N4: Launchpad2.pin_37, S3.Pin_1, S3.Pin_2, R3.Pin_1
  N5: Launchpad2.pin_38, LCM1602_IIC1.SDA
  N6: L298N1.OUT1, M1.pin_2
  N7: L298N1.OUT2, R20.Pin_1
  12V: L298N1.12V, Power_plug1.VCC
  GND_2: L298N1.GND, Power_plug1.GND
  VSS: LCD1.VSS, LCM1602_IIC1.VSS
  VDD: LCD1.VDD, LCM1602_IIC1.VDD
  N8: LCD1.V0, LCM1602_IIC1.V0
  N9: LCD1.RS, LCM1602_IIC1.RS
  N10: LCD1.R/W, LCM1602_IIC1.RW
  N11: LCD1.E, LCM1602_IIC1.E
  N12: LCD1.DB0, LCM1602_IIC1.D0
  N13: LCD1.DB1, LCM1602_IIC1.D1
  N14: LCD1.DB2, LCM1602_IIC1.D2
  N15: LCD1.DB3, LCM1602_IIC1.D3
  N16: LCD1.DB4, LCM1602_IIC1.D4
  N17: LCD1.DB5, LCM1602_IIC1.D5
  N18: LCD1.DB6, LCM1602_IIC1.D6
  N19: LCD1.DB7, LCM1602_IIC1.D7
  N20: LCD1.LED+, LCM1602_IIC1.A
  N21: LCD1.LED-, LCM1602_IIC1.K
  VCC: LCM1602_IIC1.VCC, S1.Pin_3, S1.Pin_4, S2.Pin_3, S2.Pin_4, S3.Pin_3, S3.Pin_4, Power_plug2.VCC
  N22: R1.Pin_1, R15.Pin_1
  N23: M1.pin_1, R20.Pin_0

notes:
  12V Adapter
  5V Power Source
  Passenger Button
  Driver Button
  Window Lock Switch
  Driver Down
  Driver Up
  Passenger Up
  Passenger Down
  LCD 1602 I2C
  L298N Motor Driver
  Tiva C LaunchPad
  Rotary Encoder
  Upper Limit Button
  Lower Limit Button
  Obstacle Detection Button
  DC Motor

custom parts:
  L298N DC motor driver: 2x DC motor driver with 78M05 positive voltage regulator (7..35 V) L298N: max 46 V, 2 A Set 5 V Enable jumper to enable 5 V regultor (needed for the L298N) and +5 V output at screw terminal or supply external +5 V at screw terminal Set ENA and/or ENB to +5 V to enable motor permanently or supply ENA and/or ENB with PWM signal IN1 and IN2 set rotation directory for motor A (OUT1/OUT2) IN2 and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
  LCM1602 IIC: I2C-Module to use a 1602 or 2004 LCD on with the wire.h libory Serial LCD Modul
  220 Ω Resistor: A generic resistor (0.25W)
  220 Ω Resistor: A generic resistor (0.25W)
  Rotary Encoder: Rotary Encoder from ALPS STEC12E07.
